# Fritzing sketch EngineHat (saved by Fritzing 0.9.4)
circuit board: 2.83633cm x 2.56822cm

parts:
  Power- = female pin header, 2 pins [form="♀ (female)"]
  Tach+ = female pin header, 3 pins [form="♀ (female)"]
  Battery+ = female pin header, 2 pins [form="♀ (female)"]
  Smoke = female pin header, 1 pin [form="♀ (female)"]
  Motor- = female pin header, 2 pins [form="♀ (female)"]
  Rear+ = female pin header, 2 pins [form="♀ (female)"]
  Cab+ = female pin header, 2 pins [form="♀ (female)"]
  Front+ = female pin header, 2 pins [form="♀ (female)"]
  RRO = Resistor [tolerance=±5% resistance=22k package=THT]
  WeMos_D1_Mini_Protoboard_Shield1 = WeMos D1 Mini Protoboard Shield
  BrBO = Resistor [tolerance=±5% resistance=10k package=THT]
  BrBY = Resistor [tolerance=±5% resistance=100k package=THT]

nets:
  N1: Power-.pin1, WeMos_D1_Mini_Protoboard_Shield1.5V, WeMos_D1_Mini_Protoboard_Shield1.X7-Y8
  N2: Power-.pin2, Tach+.pin2, Battery+.pin2, Rear+.pin2, Cab+.pin2, Front+.pin2, RRO.Pin_1, WeMos_D1_Mini_Protoboard_Shield1.G, WeMos_D1_Mini_Protoboard_Shield1.X3-Y1, WeMos_D1_Mini_Protoboard_Shield1.X3-Y7, WeMos_D1_Mini_Protoboard_Shield1.X3-Y10, WeMos_D1_Mini_Protoboard_Shield1.X5-Y10, WeMos_D1_Mini_Protoboard_Shield1.X6-Y1, WeMos_D1_Mini_Protoboard_Shield1.X7-Y7, WeMos_D1_Mini_Protoboard_Shield1.X7-Y10
  N3: Tach+.pin1, WeMos_D1_Mini_Protoboard_Shield1.3V3, WeMos_D1_Mini_Protoboard_Shield1.X2-Y8, WeMos_D1_Mini_Protoboard_Shield1.X3-Y8, WeMos_D1_Mini_Protoboard_Shield1.X4-Y9, BrBO.Pin_1
  N4: Tach+.pin3, WeMos_D1_Mini_Protoboard_Shield1.D6, WeMos_D1_Mini_Protoboard_Shield1.X2-Y5, WeMos_D1_Mini_Protoboard_Shield1.X3-Y6, WeMos_D1_Mini_Protoboard_Shield1.X4-Y5, BrBO.Pin_0
  N5: Battery+.pin1, WeMos_D1_Mini_Protoboard_Shield1.X3-Y2, WeMos_D1_Mini_Protoboard_Shield1.X5-Y2, BrBY.Pin_0
  N6: Smoke.pin1, WeMos_D1_Mini_Protoboard_Shield1.D5, WeMos_D1_Mini_Protoboard_Shield1.X2-Y4
  N7: Motor-.pin1, WeMos_D1_Mini_Protoboard_Shield1.D2, WeMos_D1_Mini_Protoboard_Shield1.X7-Y4
  N8: Motor-.pin2, WeMos_D1_Mini_Protoboard_Shield1.D1, WeMos_D1_Mini_Protoboard_Shield1.X7-Y3
  N9: Rear+.pin1, WeMos_D1_Mini_Protoboard_Shield1.D8, WeMos_D1_Mini_Protoboard_Shield1.X2-Y7, WeMos_D1_Mini_Protoboard_Shield1.X3-Y11
  N10: Cab+.pin1, WeMos_D1_Mini_Protoboard_Shield1.D3, WeMos_D1_Mini_Protoboard_Shield1.X5-Y11, WeMos_D1_Mini_Protoboard_Shield1.X7-Y5
  N11: Front+.pin1, WeMos_D1_Mini_Protoboard_Shield1.D7, WeMos_D1_Mini_Protoboard_Shield1.X2-Y6, WeMos_D1_Mini_Protoboard_Shield1.X7-Y11
  N12: RRO.Pin_0, WeMos_D1_Mini_Protoboard_Shield1.A0, WeMos_D1_Mini_Protoboard_Shield1.X2-Y2, WeMos_D1_Mini_Protoboard_Shield1.X5-Y6, WeMos_D1_Mini_Protoboard_Shield1.X6-Y5, BrBY.Pin_1
