# Fritzing sketch WhistleControllerWithESP8266 (saved by Fritzing 0.9.4)
breadboards: 1

parts:
  D1 = Diode [package=diode-1n4148]
  D2 = Diode [package=diode-1n4148]
  D3 = Diode [package=diode-1n4148]
  D4 = Diode [package=diode-1n4148]
  D5 = Diode [package=diode-1n4148]
  D6 = Diode [package=diode-1n4148]
  D7 = Diode [package=diode-1n4148]
  D8 = Diode [package=diode-1n4148]
  D9 = Diode [package=diode-1n4148]
  D10 = Diode [package=diode-1n4148]
  D11 = Diode [package=diode-1n4148]
  D12 = Diode [package=diode-1n4148]
  V1 = AC Power [voltage=14 frequency=60]
  R1 = Resistor [tolerance=±5% resistance=1k package="2512 [SMD]"]
  Q1 = TRANSISTOR_NPN [package=to-92]
  R2 = Resistor [tolerance=±5% resistance=1k package="2512 [SMD]"]
  V2 = DC Power [voltage=5V]
  Q2 = TRANSISTOR_NPN [package=to-92]
  R3 = Resistor [tolerance=±5% resistance=1k package="2512 [SMD]"]
  U1 = NodeMCU V3.0

nets:
  N1: D1.A, D2.C
  GND: D1.C, D7.A, V1.V-, Q1.E, V2.V-, Q2.E, U1.GND#6, U1.GND#13, U1.GND#16, U1.GND#33
  N2: D2.A, D3.C
  N3: D3.A, D4.C
  N4: D4.A, D5.C
  N5: D5.A, D6.C, Q2.C
  N6: D6.A, D12.C, R1.Pin_0
  N7: D7.C, D8.A
  N8: D8.C, D9.A
  N9: D9.C, D10.A
  N10: D10.C, D11.A
  N11: D11.C, D12.A, Q1.C
  N12: V1.V+, R1.Pin_1
  N13: Q1.B, R2.Pin_1
  N14: R2.Pin_0, U1.D5
  N15: V2.V+, U1.Vin
  N16: Q2.B, R3.Pin_1
  N17: R3.Pin_0, U1.D6

custom parts:
  NodeMCU V3.0: ESP8266 based NodeMCU
