# Fritzing sketch WhistleControllerWithTransistors (saved by Fritzing 0.9.4)
breadboards: 1

parts:
  D1 = Diode [package=diode-1n4148]
  D2 = Diode [package=diode-1n4148]
  D3 = Diode [package=diode-1n4148]
  D4 = Diode [package=diode-1n4148]
  D5 = Diode [package=diode-1n4148]
  D6 = Diode [package=diode-1n4148]
  D7 = Diode [package=diode-1n4148]
  D8 = Diode [package=diode-1n4148]
  D9 = Diode [package=diode-1n4148]
  D10 = Diode [package=diode-1n4148]
  D11 = Diode [package=diode-1n4148]
  D12 = Diode [package=diode-1n4148]
  V1 = AC Power [voltage=14 frequency=60]  # not connected
  R1 = Resistor [tolerance=±5% resistance=1k package="2512 [SMD]"]
  Q1 = TRANSISTOR_NPN [package=to-92]
  R2 = Resistor [tolerance=±5% resistance=1k package="2512 [SMD]"]
  V2 = DC Power [voltage=3.3V]  # not connected
  U3 = SWITCH-SPST-2 [package=switch-spst-vertical]
  Q2 = TRANSISTOR_NPN [package=to-92]
  R3 = Resistor [tolerance=±5% resistance=1k package="2512 [SMD]"]
  U4 = SWITCH-SPST-2 [package=switch-spst-vertical]

nets (from the breadboard view):
  N1: D1.A, D2.C
  N2: D1.C, D7.A, Q1.E, U3.P, Q2.E, U4.P
  N3: D2.A, D3.C
  N4: D3.A, D4.C
  N5: D4.A, D5.C
  N6: D5.A, D6.C, Q2.C
  N7: D6.A, D12.C, R1.Pin_0
  N8: D7.C, D8.A
  N9: D8.C, D9.A
  N10: D9.C, D10.A
  N11: D10.C, D11.A
  N12: D11.C, D12.A, Q1.C
  N13: Q1.B, R2.Pin_1
  N14: R2.Pin_0, U3.O
  N15: Q2.B, R3.Pin_1
  N16: R3.Pin_0, U4.O
