# Fritzing sketch PowerSupply (saved by Fritzing 0.9.4)
circuit board: 4.49661cm x 1.70282cm
stripboards: 1

parts:
  Rect = Bridge Rectifier [part_number=KBP307 package=THT]
  5V3 = female pin header, 2 pins [form="♀ (female)"]
  5V2 = female pin header, 2 pins [form="♀ (female)"]
  16V3 = female pin header, 2 pins [form="♀ (female)"]
  16V1 = female pin header, 2 pins [form="♀ (female)"]
  16V2 = female pin header, 2 pins [form="♀ (female)"]
  TP = male pin header, 2 pins [form="♂ (male)"]
  5V1 = female pin header, 2 pins [form="♀ (female)"]
  Buck = Adafruit LM3671 Buck Converter [part_number="Weewooday 4R7"]
  C1000-25 = Electrolytic Capacitor [capacitance=1000μF voltage=35V package="200 mil [THT, electrolytic]"]

nets:
  N1: Rect.Pin_1, 16V3.pin1, 16V1.pin1, 16V2.pin1, Buck.3.3V, C1000-25.+
  N2: Rect.Pin_4, 5V3.pin2, 5V2.pin2, 16V3.pin2, 16V1.pin2, 16V2.pin2, 5V1.pin2, Buck.VIN, C1000-25.-
  N3: Rect.Pin_3, TP.pin2
  N4: Rect.Pin_2, TP.pin1
  N5: 5V3.pin1, 5V2.pin1, 5V1.pin1, Buck.EN

notes:
  The left power bus is for track voltage (16V) rectified to DC.
  The second power bus is for 5V DC, and a connector comes back to it from the motor controller 5V output.

custom parts:
  Bridge Rectifier: Bridge Rectifier Single Phase Standard 600V Through Hole KBPM
  Adafruit LM3671 Buck Converter: Your power supply problems just got SUPER SOLVED! This 3.3V Buck Converter Breakout board is great for supplying power to low voltage circuits from a single Li-Ion cell battery or USB power. This chip provides up to 600-mA load current across the entire input voltage range of 3.5 to 5.5V. Great for your portable project, we made this "pin compatible" with the LM1117-3.3V TO-220 chip so you can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
