# Fritzing sketch SoundHat (saved by Fritzing 0.9.4)
circuit board: 2.8575cm x 2.59cm

parts:
  MAX98357 = Adafruit MAX98357A I2S 3W Class D Amplifier [part_number="Adafruit #3006"]
  +5V_- = female pin header, 2 pins [form="♀ (female)"]
  WeMos_D1_Mini_Protoboard_Shield1 = WeMos D1 Mini Protoboard Shield

nets:
  VIN: MAX98357.VIN, WeMos_D1_Mini_Protoboard_Shield1.3V3, WeMos_D1_Mini_Protoboard_Shield1.X2-Y8
  N1: MAX98357.GND, MAX98357.GAIN, +5V_-.pin2, WeMos_D1_Mini_Protoboard_Shield1.G, WeMos_D1_Mini_Protoboard_Shield1.X5-Y10, WeMos_D1_Mini_Protoboard_Shield1.X7-Y7
  N2: MAX98357.DIN, WeMos_D1_Mini_Protoboard_Shield1.RX, WeMos_D1_Mini_Protoboard_Shield1.X7-Y2
  N3: MAX98357.BCLK, WeMos_D1_Mini_Protoboard_Shield1.D8, WeMos_D1_Mini_Protoboard_Shield1.X2-Y7
  N4: MAX98357.LRCLK, WeMos_D1_Mini_Protoboard_Shield1.D4, WeMos_D1_Mini_Protoboard_Shield1.X7-Y6
  N5: +5V_-.pin1, WeMos_D1_Mini_Protoboard_Shield1.5V, WeMos_D1_Mini_Protoboard_Shield1.X5-Y11, WeMos_D1_Mini_Protoboard_Shield1.X7-Y8

custom parts:
  Adafruit MAX98357A I2S 3W Class D Amplifier: Listen to this good news - we now have an all in one digital audio amp breakout board that works incredibly well with the Raspberry Pi! If you're looking for an easy and low cost way to get you digital sound files bumpin' then the MAX08357 I2S Amp Breakout is for you. It takes standard I2S digital audio input and, not only decodes it into analog, but also amplifies it directly into a speaker.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
