# Fritzing sketch WhistleControllerWithButtons (saved by Fritzing 0.9.4)
breadboards: 1

parts:
  D1 = Diode [package=diode-1n4148]
  D2 = Diode [package=diode-1n4148]
  D3 = Diode [package=diode-1n4148]
  D4 = Diode [package=diode-1n4148]
  D5 = Diode [package=diode-1n4148]
  D6 = Diode [package=diode-1n4148]
  D7 = Diode [package=diode-1n4148]
  D8 = Diode [package=diode-1n4148]
  D9 = Diode [package=diode-1n4148]
  D10 = Diode [package=diode-1n4148]
  D11 = Diode [package=diode-1n4148]
  D12 = Diode [package=diode-1n4148]
  U1 = SWITCH-SPST-2 [package=switch-spst-vertical]
  V1 = AC Power [voltage=14 frequency=60]
  R1 = Resistor [tolerance=±5% resistance=1k package="2512 [SMD]"]
  U2 = SWITCH-SPST-2 [package=switch-spst-vertical]

nets:
  N1: D1.A, D2.C
  GND: D1.C, D7.A, U1.P, V1.V-, U2.P
  N2: D2.A, D3.C
  N3: D3.A, D4.C
  N4: D4.A, D5.C
  N5: D5.A, D6.C, U2.O
  N6: D6.A, D12.C, R1.Pin_0
  N7: D7.C, D8.A
  N8: D8.C, D9.A
  N9: D9.C, D10.A
  N10: D10.C, D11.A
  N11: D11.C, D12.A, U1.O
  N12: V1.V+, R1.Pin_1
